// Logisim project ax8.circ as structural Verilog: 8 circuits, main circuit full_adder
module main (
);

  wire clock_1_out, clock_2_out, clock_3_out, d_flipflop_1_nq, d_flipflop_1_q, d_latch_1_nq, d_latch_1_q,
       dipswitch_5_p1, dipswitch_6_p1, dipswitch_8_p1, dipswitch_9_p1, dipswitch_10_p1, dipswitch_11_p1,
       dipswitch_12_p1, dipswitch_13_p1, dipswitch_14_p1, dipswitch_15_p1, dipswitch_16_p1,
       full_adder_1_cout, full_adder_1_y, mux_2x1_1_p3, ripple_adder_4_1_cout, ripple_adder_8_1_cout;
  wire [3:0] register_8_1_q, register_8_1_q_2, ripple_adder_4_1_y, undriven_2, undriven_5;
  wire [7:0] ripple_adder_8_1_y, undriven, undriven_3, undriven_4;

  // DipSwitch dipswitch_1: pin names not known
  // DipSwitch #(.number(4)) dipswitch_2: pin names not known
  // DipSwitch dipswitch_3: pin names not known
  // DipSwitch #(.number(4)) dipswitch_4: pin names not known
  // DipSwitch #(.number(1)) dipswitch_5: pin names not known; wires that end beside it: dipswitch_5_p1
  // DipSwitch #(.number(1)) dipswitch_6: pin names not known; wires that end beside it: dipswitch_6_p1
  Clock clock_1 (.out(clock_1_out));
  // DipSwitch dipswitch_7: pin names not known
  // DipSwitch #(.number(1)) dipswitch_8: pin names not known; wires that end beside it: dipswitch_8_p1
  // DipSwitch #(.number(1)) dipswitch_9: pin names not known; wires that end beside it: dipswitch_9_p1
  // DipSwitch #(.number(1)) dipswitch_10: pin names not known; wires that end beside it: dipswitch_10_p1
  // DipSwitch #(.number(1)) dipswitch_11: pin names not known; wires that end beside it: dipswitch_11_p1
  Hex_Digit_Display #(.decimalPoint("false")) hex_digit_display_1 (.value(ripple_adder_8_1_y[7:4]));
  ripple_adder_8 ripple_adder_8_1 (
    .A(undriven), .B(undriven_4), .Cin(dipswitch_9_p1), .Y(ripple_adder_8_1_y), .Cout(ripple_adder_8_1_cout));
  LED led_1 (.in(ripple_adder_8_1_cout));
  Hex_Digit_Display #(.decimalPoint("false")) hex_digit_display_2 (.value(ripple_adder_4_1_y));
  ripple_adder_4 ripple_adder_4_1 (
    .A(undriven_2), .B(undriven_5), .Cin(dipswitch_10_p1), .Y(ripple_adder_4_1_y),
    .Cout(ripple_adder_4_1_cout));
  LED led_2 (.in(ripple_adder_4_1_cout));
  LED led_3 (.in(full_adder_1_y));
  full_adder full_adder_1 (
    .A(dipswitch_5_p1), .B(dipswitch_6_p1), .Cin(dipswitch_11_p1), .Y(full_adder_1_y),
    .Cout(full_adder_1_cout));
  LED led_4 (.in(full_adder_1_cout));
  Hex_Digit_Display #(.decimalPoint("false")) hex_digit_display_3 (.value(register_8_1_q_2));
  Hex_Digit_Display #(.decimalPoint("false")) hex_digit_display_4 (.value(register_8_1_q));
  register_8 register_8_1 (
    .CLK(clock_1_out), .WE(dipswitch_8_p1), .D(undriven_3), .Q({register_8_1_q_2, register_8_1_q}));
  Hex_Digit_Display #(.decimalPoint("false")) hex_digit_display_5 (.value(ripple_adder_8_1_y[3:0]));
  // DipSwitch #(.number(1)) dipswitch_12: pin names not known; wires that end beside it: dipswitch_12_p1
  // DipSwitch #(.number(1)) dipswitch_13: pin names not known; wires that end beside it: dipswitch_13_p1
  Clock clock_2 (.out(clock_2_out));
  Clock clock_3 (.out(clock_3_out));
  LED led_5 (.in(d_latch_1_q));
  d_latch d_latch_1 (.D(dipswitch_12_p1), .CLK(clock_2_out), .Q(d_latch_1_q), .NQ(d_latch_1_nq));
  LED led_6 (.in(d_latch_1_nq));
  LED led_7 (.in(d_flipflop_1_q));
  d_flipflop d_flipflop_1 (.D(dipswitch_13_p1), .CLK(clock_3_out), .Q(d_flipflop_1_q), .NQ(d_flipflop_1_nq));
  LED led_8 (.in(d_flipflop_1_nq));
  // DipSwitch #(.number(1)) dipswitch_14: pin names not known; wires that end beside it: dipswitch_14_p1
  // DipSwitch #(.number(1)) dipswitch_15: pin names not known; wires that end beside it: dipswitch_15_p1
  // DipSwitch #(.number(1)) dipswitch_16: pin names not known; wires that end beside it: dipswitch_16_p1, dipswitch_16_p1
  LED led_9 (.in(mux_2x1_1_p3));
  // mux_2x1 mux_2x1_1: pin names not known; wires that end beside it: dipswitch_15_p1, dipswitch_14_p1, mux_2x1_1_p3

  // Notes on the sheet:
  //   Test: Ripple Adder with 8-bits
  //   Test: Ripple Adder with 4-bits
  //   Test: Full Adder
  //   Test: Register of 8-bits
  //   Test: D-Latch
  //   Test: D Flip Flop
  //   Test: Multiplexer 2 to 1
endmodule

module full_adder (
  input  A,
  input  B,
  input  Cin,
  output Y,
  output Cout
);

  wire and_1_out, and_2_out, xor_1_out;

  xor xor_1 (xor_1_out, A, B);
  and and_1 (and_1_out, xor_1_out, Cin);
  and and_2 (and_2_out, A, B);
  xor xor_2 (Y, xor_1_out, Cin);
  or or_1 (Cout, and_1_out, and_2_out);
endmodule

module ripple_adder_4 (
  input  [3:0] A,
  input  [3:0] B,
  input  Cin,
  output [3:0] Y,
  output Cout
);

  wire full_adder_1_cout, full_adder_2_cout, full_adder_3_cout;

  full_adder full_adder_1 (.A(A[0]), .B(B[0]), .Cin(Cin), .Y(Y[0]), .Cout(full_adder_1_cout));
  full_adder full_adder_2 (.A(A[1]), .B(B[1]), .Cin(full_adder_1_cout), .Y(Y[1]), .Cout(full_adder_2_cout));
  full_adder full_adder_3 (.A(A[2]), .B(B[2]), .Cin(full_adder_2_cout), .Y(Y[2]), .Cout(full_adder_3_cout));
  full_adder full_adder_4 (.A(A[3]), .B(B[3]), .Cin(full_adder_3_cout), .Y(Y[3]), .Cout(Cout));
endmodule

module ripple_adder_8 (
  input  [7:0] A,
  input  [7:0] B,
  input  Cin,
  output [7:0] Y,
  output Cout
);

  wire ripple_adder_4_1_cout;

  ripple_adder_4 ripple_adder_4_1 (.A(A[3:0]), .B(B[3:0]), .Cin(Cin), .Y(Y[3:0]), .Cout(ripple_adder_4_1_cout));
  // ripple_adder_4 ripple_adder_4_2: pin names not known; wires that end beside it: A[7:4], B[7:4], ripple_adder_4_1_cout, Y[7:4], Cout
endmodule

module d_latch (
  input  D,
  input  CLK,
  output Q,
  output NQ
);

  wire nand_1_out, nand_2_out, not_1_out;

  not not_1 (not_1_out, D);
  nand nand_1 (nand_1_out, D, CLK);
  nand nand_2 (nand_2_out, CLK, not_1_out);
  nand nand_3 (Q, NQ, nand_1_out);
  nand nand_4 (NQ, nand_2_out, Q);
endmodule

module d_flipflop (
  input  D,
  input  CLK,
  output Q,
  output NQ
);

  wire Master_q, not_1_out;

  not not_1 (not_1_out, CLK);
  d_latch Master (.D(D), .CLK(not_1_out), .Q(Master_q));  // open: NQ
  d_latch Slave (.D(Master_q), .CLK(CLK), .Q(Q), .NQ(NQ));

  // Notes on the sheet:
  //   Rising edge D-FlipFlop
endmodule

module mux_2x1 (
  input  S,
  input  A,
  input  B,
  output Y
);

  wire nand_1_out, nand_3_out, not_1_out;

  not not_1 (not_1_out, S);
  nand nand_1 (nand_1_out, not_1_out, A);
  nand nand_2 (Y, nand_1_out, nand_3_out);
  nand nand_3 (nand_3_out, B, S);
endmodule

module register_8 (
  input  CLK,
  input  WE,
  input  [7:0] D,
  output [7:0] Q
);

  wire mux_2x1_1_y, mux_2x1_2_y, mux_2x1_3_y, mux_2x1_4_y, mux_2x1_5_y, mux_2x1_6_y, mux_2x1_7_y, mux_2x1_8_y;

  mux_2x1 mux_2x1_1 (.S(WE), .A(Q[0]), .B(D[0]), .Y(mux_2x1_1_y));
  mux_2x1 mux_2x1_2 (.S(WE), .A(Q[1]), .B(D[1]), .Y(mux_2x1_2_y));
  mux_2x1 mux_2x1_3 (.S(WE), .A(Q[2]), .B(D[2]), .Y(mux_2x1_3_y));
  mux_2x1 mux_2x1_4 (.S(WE), .A(Q[3]), .B(D[3]), .Y(mux_2x1_4_y));
  mux_2x1 mux_2x1_5 (.S(WE), .A(Q[4]), .B(D[4]), .Y(mux_2x1_5_y));
  mux_2x1 mux_2x1_6 (.S(WE), .A(Q[5]), .B(D[5]), .Y(mux_2x1_6_y));
  mux_2x1 mux_2x1_7 (.S(WE), .A(Q[6]), .B(D[6]), .Y(mux_2x1_7_y));
  mux_2x1 mux_2x1_8 (.S(WE), .A(Q[7]), .B(D[7]), .Y(mux_2x1_8_y));
  d_flipflop d_flipflop_1 (.Q(Q[0]));  // open: D, CLK, NQ
  d_flipflop d_flipflop_2 (.Q(Q[1]));  // open: D, CLK, NQ
  d_flipflop d_flipflop_3 (.Q(Q[2]));  // open: D, CLK, NQ
  d_flipflop d_flipflop_4 (.Q(Q[3]));  // open: D, CLK, NQ
  d_flipflop d_flipflop_5 (.Q(Q[4]));  // open: D, CLK, NQ
  d_flipflop d_flipflop_6 (.Q(Q[5]));  // open: D, CLK, NQ
  d_flipflop d_flipflop_7 (.Q(Q[6]));  // open: D, CLK, NQ
  d_flipflop d_flipflop_8 (.Q(Q[7]));  // open: D, CLK, NQ
endmodule
