// Logisim project ax8.circ as structural Verilog
module register_file (
  input  CLK,
  input  RST,
  input  [2:0] RDA_SEL,
  input  [2:0] RDB_SEL,
  input  WE,
  input  [2:0] WR_SEL,
  input  [1:0] WR_MODE,
  input  [15:0] WR_DATA,
  output [7:0] RDA_DATA,
  output [7:0] RDB_DATA,
  output [15:0] Z_DATA,
  output [15:0] SP_DATA
);

  wire adder_subtractor_8_1_cout, adder_subtractor_8_1_vout, adder_subtractor_8_2_cout,
       adder_subtractor_8_2_vout, DEC, demultiplexer_1_out1, INC, INC_CIN, IS_INC_DEC, or_3_out, or_4_out,
       or_5_out, or_6_out, WE_REG_A, WE_REG_B, WE_REG_C, WE_REG_D, WE_REG_H, WE_REG_L, WE_REG_SP, WE_REG_X,
       WE_REG_Y, WE_REG_Z, WR8, WR16;
  wire [7:0] adder_subtractor_8_2_y, HI_R16, LO_R16, multiplexer_3_out, multiplexer_4_out, multiplexer_5_out,
       multiplexer_6_out, REG_A_Q, REG_B_Q, REG_C_Q, REG_D_Q;

  Demultiplexer #(.select(2)) demultiplexer_1 (
    .out0(WR8), .out1(demultiplexer_1_out1), .out2(INC), .out3(DEC), .in(WE), .sel(WR_MODE));
  Demultiplexer #(.select(3)) demultiplexer_2 (
    .out0(WE_REG_A), .out1(WE_REG_B), .out2(WE_REG_C), .out3(WE_REG_D), .out4(WE_REG_X), .out5(WE_REG_Y),
    .out6(WE_REG_H), .out7(WE_REG_L), .in(WR8), .sel(WR_SEL));
  Demultiplexer demultiplexer_3 (.out0(WE_REG_Z), .out1(WE_REG_SP), .in(WR16), .sel(WR_SEL[0]));
  and and_1 (INC_CIN, INC, ~DEC);  // AND_Gate
  or or_1 (IS_INC_DEC, INC, DEC);
  or or_2 (WR16, demultiplexer_1_out1, INC, DEC);
  Multiplexer #(.select(3), .width(8)) multiplexer_1 (
    .in0(REG_A_Q), .in1(REG_B_Q), .in2(REG_C_Q), .in3(REG_D_Q), .in4(Z_DATA[7:0]), .in5(Z_DATA[15:8]),
    .in6(SP_DATA[15:8]), .in7(SP_DATA[7:0]), .out(RDA_DATA), .sel(RDA_SEL));
  Register reg_a (.D(WR_DATA[7:0]), .en(WE_REG_A), .clk(CLK), .Q(REG_A_Q), .clr(RST));
  Register reg_b (.D(WR_DATA[7:0]), .en(WE_REG_B), .clk(CLK), .Q(REG_B_Q), .clr(RST));
  Register reg_c (.D(WR_DATA[7:0]), .en(WE_REG_C), .clk(CLK), .Q(REG_C_Q), .clr(RST));
  Register reg_d (.D(WR_DATA[7:0]), .en(WE_REG_D), .clk(CLK), .Q(REG_D_Q), .clr(RST));
  Multiplexer #(.select(3), .width(8)) multiplexer_2 (
    .in0(REG_A_Q), .in1(REG_B_Q), .in2(REG_C_Q), .in3(REG_D_Q), .in4(Z_DATA[7:0]), .in5(Z_DATA[15:8]),
    .in6(SP_DATA[15:8]), .in7(SP_DATA[7:0]), .out(RDB_DATA), .sel(RDB_SEL));
  or or_3 (or_3_out, WE_REG_X, WE_REG_Z);
  or or_4 (or_4_out, WE_REG_H, WE_REG_SP);
  Multiplexer #(.width(8)) multiplexer_3 (
    .in0(Z_DATA[7:0]), .in1(SP_DATA[7:0]), .out(multiplexer_3_out), .sel(WR_SEL[0]));
  Multiplexer #(.width(8)) multiplexer_4 (
    .in0(Z_DATA[15:8]), .in1(SP_DATA[15:8]), .out(multiplexer_4_out), .sel(WR_SEL[0]));
  Register reg_x (.D(LO_R16), .en(or_3_out), .clk(CLK), .Q(Z_DATA[7:0]), .clr(RST));
  Register reg_l (.D(LO_R16), .en(or_4_out), .clk(CLK), .Q(SP_DATA[7:0]), .clr(RST));
  Multiplexer #(.width(8)) multiplexer_5 (
    .in0(WR_DATA[7:0]), .in1(multiplexer_3_out), .out(multiplexer_5_out), .sel(IS_INC_DEC));
  Multiplexer #(.width(8)) multiplexer_6 (
    .in0(WR_DATA[15:8]), .in1(multiplexer_4_out), .out(multiplexer_6_out), .sel(IS_INC_DEC));
  or or_5 (or_5_out, WE_REG_Y, WE_REG_Z);
  or or_6 (or_6_out, WE_REG_L, WE_REG_SP);
  Register reg_y (.D(HI_R16), .en(or_5_out), .clk(CLK), .Q(Z_DATA[15:8]), .clr(RST));
  Register reg_h (.D(HI_R16), .en(or_6_out), .clk(CLK), .Q(SP_DATA[15:8]), .clr(RST));
  adder_subtractor_8 adder_subtractor_8_1 (
    .Y(LO_R16), .COUT(adder_subtractor_8_1_cout), .VOUT(adder_subtractor_8_1_vout));  // open: A, B, CIN, MODE
  // NoConnect on adder_subtractor_8_1_vout
  adder_subtractor_8 adder_subtractor_8_2 (
    .Y(adder_subtractor_8_2_y), .COUT(adder_subtractor_8_2_cout), .VOUT(adder_subtractor_8_2_vout));  // open: A, B, CIN, MODE
  // NoConnect on adder_subtractor_8_2_cout
  // NoConnect on adder_subtractor_8_2_vout
  Multiplexer #(.width(8)) multiplexer_7 (.in0(LO_R16), .in1(adder_subtractor_8_2_y), .out(HI_R16), .sel(WR16));

  // Other names for the same wires on the sheet: REG_L_Q[7:0] = SP_DATA[7:0]; REG_H_Q[7:0] = SP_DATA[15:8];
  //   WR_DATA_L[7:0] = WR_DATA[7:0]; WR_DATA_H[7:0] = WR_DATA[15:8]; REG_X_Q[7:0] = Z_DATA[7:0];
  //   REG_Y_Q[7:0] = Z_DATA[15:8]
endmodule

module u_alu (
  input  [2:0] OP,
  input  [7:0] A,
  input  [7:0] B,
  input  CIN,
  output [7:0] Y,
  output ZF,
  output CF,
  output VF,
  output NF
);

  wire ADC_SBC_COUT, ADC_SBC_VOUT, and_2_out, and_3_out, ROT_COUT, xor_2_out;
  wire [7:0] ADC_SBC_Y, AND_Y, OR_Y, ROT_Y, XOR_Y;

  shift_rotator shift_rotator_1 (.A(A), .CIN(CIN), .DIR(OP[0]), .Y(ROT_Y), .COUT(ROT_COUT));
  assign AND_Y = A & B;  // AND_Gate and_1, 8 bits wide
  assign OR_Y = A | B;  // OR_Gate or_1, 8 bits wide
  assign XOR_Y = A ^ B;  // XOR_Gate xor_1, 8 bits wide
  adder_subtractor_8 adder_subtractor_8_1 (
    .A(A), .B(B), .CIN(CIN), .MODE(OP[0]), .Y(ADC_SBC_Y), .COUT(ADC_SBC_COUT), .VOUT(ADC_SBC_VOUT));
  xor xor_2 (xor_2_out, OP[0], OP[1]);
  and and_2 (and_2_out, ADC_SBC_COUT, ~OP[1], ~OP[2]);  // AND_Gate
  and and_3 (and_3_out, ROT_COUT, xor_2_out, OP[2]);
  Multiplexer #(.select(3), .width(8)) multiplexer_1 (
    .in0(ADC_SBC_Y), .in1(ADC_SBC_Y), .in2(AND_Y), .in3(OR_Y), .in4(XOR_Y), .in5(ROT_Y), .in6(ROT_Y),
    .in7(B), .out({NF, Y[6:0]}), .sel(OP));
  nor nor_1 (ZF, Y[0], Y[1], Y[2], Y[3], Y[4], Y[5], Y[6], NF, NF);
  or or_2 (CF, and_2_out, and_3_out);
  and and_4 (VF, ADC_SBC_VOUT, ~OP[1], ~OP[2]);  // AND_Gate

  assign Y[7] = NF;

  // Other names for the same wires on the sheet: IN_A[7:0] = A; IN_B[7:0] = B; IN_OP[2:0] = OP;
  //   Y_OUT[7:0] = {NF, Y[6:0]}
endmodule

module v_alu (
  input  CLK,
  input  RST_N,
  input  START,
  input  [1:0] OP,
  input  [7:0] A,
  input  [7:0] B,
  output [15:0] Y,
  output ZF,
  output VF,
  output NF,
  output BUSY,
  output DIV_BY_ZERO
);

  wire A_SIGN, and_1_out, B_SIGN, C0, C1, C2, IS_SIGNED, or_1_out, RST, sign_bridge_8_1_chain_out,
       sign_bridge_8_2_chain_out, sign_bridge_8_3_chain_out, T0, T1, T2, T3, xor_1_out, xor_2_out, xor_3_out,
       xor_4_out;
  wire [7:0] A_BUF_q, A_Q, A_t, B_BUF_q, B_Q, B_t, NEXT_A, NEXT_B, PRE_OUT_Y_HI, PRE_OUT_Y_LO;
  wire [15:0] MUL_Y;

  or or_1 (or_1_out, BUSY, START);
  and and_1 (and_1_out, or_1_out, ~T3);  // AND_Gate
  xor xor_1 (xor_1_out, BUSY, T0);
  and and_2 (C0, BUSY, T0);
  xor xor_2 (xor_2_out, T1, C0);
  and and_3 (C1, T1, C0);
  xor xor_3 (xor_3_out, T2, C1);
  and and_4 (C2, T2, C1);
  xor xor_4 (xor_4_out, T3, C2);
  and and_5 (A_SIGN, A[7], OP[1]);
  and and_6 (B_SIGN, B[7], OP[1]);
  not not_1 (RST, RST_N);
  D_Flip_Flop d_ff_1 (.D(and_1_out), .clk(CLK), .Q(BUSY), .reset(RST));  // open: Qn, preset
  D_Flip_Flop d_ff_2 (.D(xor_1_out), .clk(CLK), .Q(T0), .reset(RST));  // open: Qn, preset
  D_Flip_Flop d_ff_3 (.D(xor_2_out), .clk(CLK), .Q(T1), .reset(RST));  // open: Qn, preset
  D_Flip_Flop d_ff_4 (.D(xor_3_out), .clk(CLK), .Q(T2), .reset(RST));  // open: Qn, preset
  D_Flip_Flop d_ff_5 (.D(xor_4_out), .clk(CLK), .Q(T3), .reset(RST));  // open: Qn, preset
  xor xor_5 (IS_SIGNED, A_SIGN, B_SIGN);
  Register A_BUF (.D(NEXT_A), .en(1'b1), .clk(CLK), .Q(A_BUF_q), .clr(RST));
  Register B_BUF (.D(NEXT_B), .en(1'b1), .clk(CLK), .Q(B_BUF_q), .clr(RST));
  sign_bridge_8 sign_bridge_8_1 (.A(A), .CHAIN_IN(1'b1), .SIGN(A_SIGN), .Y(A_t), .CHAIN_OUT(sign_bridge_8_1_chain_out));
  // NoConnect on sign_bridge_8_1_chain_out
  sign_bridge_8 sign_bridge_8_2 (.A(B), .CHAIN_IN(1'b1), .SIGN(B_SIGN), .Y(B_t), .CHAIN_OUT(sign_bridge_8_2_chain_out));
  // NoConnect on sign_bridge_8_2_chain_out
  Multiplexer #(.width(8)) multiplexer_1 (.in0(A_t), .in1(A_BUF_q), .out(A_Q), .sel(BUSY));
  Multiplexer #(.width(8)) multiplexer_2 (.in0(B_t), .in1(B_BUF_q), .out(B_Q), .sel(BUSY));
  sign_bridge_8 sign_bridge_8_3 (
    .A(PRE_OUT_Y_LO), .CHAIN_IN(1'b1), .SIGN(IS_SIGNED), .Y(Y[7:0]), .CHAIN_OUT(sign_bridge_8_3_chain_out));
  sign_bridge_8 sign_bridge_8_4 (
    .A(PRE_OUT_Y_HI), .CHAIN_IN(sign_bridge_8_3_chain_out), .SIGN(IS_SIGNED), .Y({NF, Y[14:8]}));  // open: CHAIN_OUT
  multiplier_8 multiplier_8_1 (.CLK(CLK), .RST(RST), .IN_M(A_Q), .IN_Q(B_Q), .Y(MUL_Y), .OUT_M(NEXT_A), .OUT_Q(NEXT_B));
  nor nor_1 (ZF, Y[0], Y[1], Y[2], Y[3], Y[4], Y[5], Y[6], Y[7], Y[8], Y[9], Y[10], Y[11], Y[12], Y[13], Y[14], NF);
  Multiplexer #(.width(16)) multiplexer_3 (.in0(MUL_Y), .out({PRE_OUT_Y_HI, PRE_OUT_Y_LO}), .sel(OP[0]));  // open: in1

  assign Y[15] = NF;

  // Other names for the same wires on the sheet: IN_A[7:0] = A; IN_B[7:0] = B; IN_OP[1:0] = OP; IS_DIV = OP[0];
  //   SIGN = OP[1]; OUT_Y_LO[7:0] = Y[7:0]; OUT_Y_HI[7:0] = {NF, Y[14:8]}

  // Notes on the sheet:
  //   STATE MACHINE =>
  //   PRE SIGN CORRECTION
  //   POST SIGN CORRECTION
endmodule

module multiplier_8 (
  input  CLK,
  input  RST,
  input  [7:0] IN_M,
  input  [7:0] IN_Q,
  output [15:0] Y,
  output [7:0] OUT_M,
  output [7:0] OUT_Q
);

  wire adder_subtractor_8_1_cout, adder_subtractor_8_1_vout, adder_subtractor_8_2_cout,
       adder_subtractor_8_2_vout, shift_rotator_1_cout, shift_rotator_2_cout, shift_rotator_3_cout;
  wire [7:0] HI_Q, NEXT_HI_ACC, NEXT_HI_Q, NEXT_LO_ACC;

  Register LO_ACC (.D(NEXT_LO_ACC), .en(IN_M[0]), .clk(CLK), .Q(Y[7:0]), .clr(RST));
  Register HI_ACC (.D(NEXT_HI_ACC), .en(IN_M[0]), .clk(CLK), .Q(Y[15:8]), .clr(RST));
  Register u_HI_Q (.D(NEXT_HI_Q), .en(1'b1), .clk(CLK), .Q(HI_Q), .clr(RST));
  adder_subtractor_8 adder_subtractor_8_1 (
    .A(Y[7:0]), .B(IN_Q), .CIN(1'b0), .MODE(1'b0), .Y(NEXT_LO_ACC), .COUT(adder_subtractor_8_1_cout),
    .VOUT(adder_subtractor_8_1_vout));
  // NoConnect on adder_subtractor_8_1_vout
  adder_subtractor_8 adder_subtractor_8_2 (
    .A(Y[15:8]), .B(HI_Q), .CIN(adder_subtractor_8_1_cout), .MODE(1'b0), .Y(NEXT_HI_ACC),
    .COUT(adder_subtractor_8_2_cout), .VOUT(adder_subtractor_8_2_vout));
  // NoConnect on adder_subtractor_8_2_cout
  // NoConnect on adder_subtractor_8_2_vout
  shift_rotator shift_rotator_1 (.A(IN_M), .CIN(1'b0), .DIR(1'b0), .Y(OUT_M), .COUT(shift_rotator_1_cout));
  // NoConnect on shift_rotator_1_cout
  shift_rotator shift_rotator_2 (.A(IN_Q), .CIN(1'b0), .DIR(1'b1), .Y(OUT_Q), .COUT(shift_rotator_2_cout));
  shift_rotator shift_rotator_3 (
    .A(HI_Q), .CIN(shift_rotator_2_cout), .DIR(1'b1), .Y(NEXT_HI_Q), .COUT(shift_rotator_3_cout));
  // NoConnect on shift_rotator_3_cout

  // Other names for the same wires on the sheet: M_LSB = IN_M[0]; LO_Q[7:0] = IN_Q; LO_ACC[7:0] = Y[7:0];
  //   HI_ACC[7:0] = Y[15:8]
endmodule

module adder_subtractor_8 (
  input  [7:0] A,
  input  [7:0] B,
  input  CIN,
  input  MODE,
  output [7:0] Y,
  output COUT,
  output VOUT
);

  wire B0, B1, B2, B3, B4, B5, B6, B7, full_adder_1_cout, full_adder_2_cout, full_adder_3_cout,
       full_adder_4_cout, full_adder_5_cout, full_adder_6_cout, full_adder_7_cout;

  assign {B7, B6, B5, B4, B3, B2, B1, B0} = B ^ {8{MODE}};  // XOR_Gate xor_1, 8 bits wide
  full_adder full_adder_1 (.A(A[0]), .B(B0), .CIN(CIN), .Y(Y[0]), .COUT(full_adder_1_cout));
  full_adder full_adder_2 (.A(A[1]), .B(B1), .CIN(full_adder_1_cout), .Y(Y[1]), .COUT(full_adder_2_cout));
  full_adder full_adder_3 (.A(A[2]), .B(B2), .CIN(full_adder_2_cout), .Y(Y[2]), .COUT(full_adder_3_cout));
  full_adder full_adder_4 (.A(A[3]), .B(B3), .CIN(full_adder_3_cout), .Y(Y[3]), .COUT(full_adder_4_cout));
  full_adder full_adder_5 (.A(A[4]), .B(B4), .CIN(full_adder_4_cout), .Y(Y[4]), .COUT(full_adder_5_cout));
  full_adder full_adder_6 (.A(A[5]), .B(B5), .CIN(full_adder_5_cout), .Y(Y[5]), .COUT(full_adder_6_cout));
  full_adder full_adder_7 (.A(A[6]), .B(B6), .CIN(full_adder_6_cout), .Y(Y[6]), .COUT(full_adder_7_cout));
  full_adder full_adder_8 (.A(A[7]), .B(B7), .CIN(full_adder_7_cout), .Y(Y[7]), .COUT(COUT));
  xor xor_2 (VOUT, full_adder_7_cout, COUT);
endmodule

module full_adder (
  input  A,
  input  B,
  input  CIN,
  output Y,
  output COUT
);

  wire and_1_out, and_2_out, xor_1_out;

  xor xor_1 (xor_1_out, A, B);
  and and_1 (and_1_out, xor_1_out, CIN);
  and and_2 (and_2_out, A, B);
  xor xor_2 (Y, xor_1_out, CIN);
  or or_1 (COUT, and_1_out, and_2_out);
endmodule

module shift_rotator (
  input  [7:0] A,
  input  CIN,
  input  DIR,
  output [7:0] Y,
  output COUT
);

  Multiplexer multiplexer_1 (.in0(A[1]), .in1(CIN), .out(Y[0]), .sel(DIR));
  Multiplexer multiplexer_2 (.in0(A[5]), .in1(A[3]), .out(Y[4]), .sel(DIR));
  Multiplexer multiplexer_3 (.in0(A[0]), .in1(A[7]), .out(COUT), .sel(DIR));
  Multiplexer multiplexer_4 (.in0(A[2]), .in1(A[0]), .out(Y[1]), .sel(DIR));
  Multiplexer multiplexer_5 (.in0(A[3]), .in1(A[1]), .out(Y[2]), .sel(DIR));
  Multiplexer multiplexer_6 (.in0(A[6]), .in1(A[4]), .out(Y[5]), .sel(DIR));
  Multiplexer multiplexer_7 (.in0(A[7]), .in1(A[5]), .out(Y[6]), .sel(DIR));
  Multiplexer multiplexer_8 (.in0(A[4]), .in1(A[2]), .out(Y[3]), .sel(DIR));
  Multiplexer multiplexer_9 (.in0(CIN), .in1(A[6]), .out(Y[7]), .sel(DIR));
endmodule

module sign_bridge_8 (
  input  [7:0] A,
  input  CHAIN_IN,
  input  SIGN,
  output [7:0] Y,
  output CHAIN_OUT
);

  wire and_1_out, and_2_out, and_3_out, and_4_out, and_5_out, and_6_out, and_7_out, and_8_out, N_CIN,
       or_1_out, or_2_out, or_3_out, or_4_out, or_5_out, or_6_out, or_7_out, or_8_out;

  not not_1 (N_CIN, CHAIN_IN);
  or or_1 (or_1_out, A[0], N_CIN);
  or or_2 (or_2_out, A[0], N_CIN, A[1]);
  or or_3 (or_3_out, or_2_out, N_CIN, A[2]);
  or or_4 (or_4_out, or_3_out, N_CIN, A[3]);
  or or_5 (or_5_out, or_4_out, N_CIN, A[4]);
  or or_6 (or_6_out, or_5_out, N_CIN, A[5]);
  or or_7 (or_7_out, or_6_out, N_CIN, A[6]);
  or or_8 (or_8_out, or_7_out, A[7]);
  and and_1 (and_1_out, N_CIN, SIGN);
  and and_2 (and_2_out, or_1_out, SIGN);
  and and_3 (and_3_out, or_2_out, SIGN);
  and and_4 (and_4_out, or_3_out, SIGN);
  and and_5 (and_5_out, or_4_out, SIGN);
  and and_6 (and_6_out, or_5_out, SIGN);
  and and_7 (and_7_out, or_6_out, SIGN);
  and and_8 (and_8_out, or_7_out, SIGN);
  and and_9 (CHAIN_OUT, or_8_out, N_CIN);
  xor xor_1 (Y[0], A[0], and_1_out);
  xor xor_2 (Y[1], A[1], and_2_out);
  xor xor_3 (Y[2], A[2], and_3_out);
  xor xor_4 (Y[3], A[3], and_4_out);
  xor xor_5 (Y[4], A[4], and_5_out);
  xor xor_6 (Y[5], A[5], and_6_out);
  xor xor_7 (Y[6], A[6], and_7_out);
  xor xor_8 (Y[7], A[7], and_8_out);

  // Other names for the same wires on the sheet: COUT = CHAIN_OUT

  // Notes on the sheet:
  //   Only convert if in chained mode. 
  //   Keep chain if all bit were zero in this byte
endmodule
